# Fritzing sketch RasPiZeroFuelMiser14 (saved by Fritzing 0.9.2b)
circuit board: 9.06207cm x 4.03066cm
breadboards: 1

parts:
  J1 = female pin header, 2 pins [form="♀ (female)"]
  J2 = female pin header, 2 pins [form="♀ (female)"]
  J3 = female pin header, 2 pins [form="♀ (female)"]
  J4 = female pin header, 2 pins [form="♀ (female)"]
  J5 = female pin header, 2 pins [form="♀ (female)"]  # not connected
  J6 = female pin header, 2 pins [form="♀ (female)"]
  J8 = female pin header, 2 pins [form="♀ (female)"]
  J9 = female pin header, 2 pins [form="♀ (female)"]
  J10 = female pin header, 2 pins [form="♀ (female)"]
  J11 = female pin header, 2 pins [form="♀ (female)"]
  J12 = female pin header, 2 pins [form="♀ (female)"]
  J13 = female pin header, 2 pins [form="♀ (female)"]
  J15 = female pin header, 2 pins [form="♀ (female)"]
  J16 = female pin header, 2 pins [form="♀ (female)"]
  J18 = female pin header, 2 pins [form="♀ (female)"]
  S3 = Pushbutton [package=THT]
  S2 = Pushbutton [package=THT]
  R5 = Resistor [tolerance=±5% resistance=220 package=THT]
  R4 = Resistor [tolerance=±5% resistance=220 package=THT]
  Q1 = NPN-Transistor [package="TO92 [THT]"]
  C2 = Electrolytic Capacitor [capacitance=22µF voltage=16V package="100 mil [THT, electrolytic]"]
  R3 = Resistor [tolerance=±5% resistance=220 package=THT]
  LED1 = LED - 5mm [color="Red (633nm)" package="5 mm [THT]"]
  S1 = Pushbutton [package=THT]
  J17 = female pin header, 2 pins [form="♀ (female)"]
  R2 = Resistor [tolerance=±5% resistance=220 package=THT]
  R1 = Resistor [tolerance=±5% resistance=220 package=THT]
  C1 = Electrolytic Capacitor [capacitance=22µF voltage=16V package="100 mil [THT, electrolytic]"]

nets:
  N1: J1.pin1, R1.Pin_0
  N2: J1.pin2, R2.Pin_0
  N3: J2.pin1, J4.pin2
  N4: J2.pin2, J12.pin1, J17.pin2
  N5: J3.pin1, J10.pin2
  N6: J3.pin2, J6.pin2
  N7: J4.pin1, J11.pin2
  N8: J8.pin1, S2.leg0, R5.Pin_0, Q1.C, C2.-, LED1.cathode, S1.leg0
  N9: J8.pin2, R4.Pin_0
  N10: J9.pin1, J18.pin1
  N11: J10.pin1, R3.Pin_1
  N12: J11.pin1, J13.pin1
  N13: J12.pin2, S3.leg0
  N14: J15.pin1, J17.pin1
  N15: J15.pin2, J16.pin2, C1.+
  N16: J16.pin1, Q1.E, C1.-
  N17: J18.pin2, C2.+, R3.Pin_0, LED1.anode
  N18: S3.leg1, R5.Pin_1
  N19: S2.leg1, R4.Pin_1
  N20: Q1.B, R1.Pin_1
  N21: S1.leg1, R2.Pin_1

notes:
  KH2016 V14.0
